# Fritzing sketch PCBv3 (saved by Fritzing 0.9.9b)
circuit board: 15cm x 10cm
breadboards: 1

parts:
  A1 = FRDM-KL25Z [part_number=FRDM-KL25Z]
  J1 = Terminal Block - 3 pins [package=THT]
  J2 = Terminal Block - 3 pins [package=THT]
  J3 = Terminal Block - 3 pins [package=THT]
  J4 = Terminal Block - 2 pins [package=THT]
  J5 = Terminal Block - 3 pins [package=THT]
  J6 = Terminal Block - 2 pins [package=THT]
  J8 = Terminal Block - 3 pins [package=THT]
  J9 = Terminal Block - 3 pins [package=THT]
  J10 = Terminal Block - 2 pins [package=THT]
  J11 = Terminal Block - 3 pins [package=THT]
  J12 = Terminal Block - 2 pins [package=THT]
  J13 = Terminal Block - 2 pins [package=THT]

nets:
  N1: A1.PTC0, J11.Line_1
  N2: A1.PTA12, J6.Line_1
  N3: A1.PTA4, J6.Line_2
  N4: A1.PTA5, J5.Line_1
  N5: A1.PTC8, J5.Line_2
  N6: A1.PTC9, J5.Line_3
  N7: A1.PTA13, J4.Line_1
  N8: A1.PTD5, J4.Line_2
  N9: A1.PTD0, J3.Line_1
  N10: A1.PTD2, J3.Line_2
  N11: A1.PDT3, J3.Line_3
  N12: A1.PTD1, J2.Line_2
  N13: A1.PTE31, J2.Line_1
  N14: A1.GND, J13.Line_1
  N15: A1.PTD6, J1.Line_1
  N16: A1.PTE0, J2.Line_3
  N17: A1.PTD7, J1.Line_2
  N18: A1.PTE1, J1.Line_3
  N19: A1.PTB8, J8.Line_1
  N20: A1.PTB9, J8.Line_2
  N21: A1.PTB10, J8.Line_3
  N22: A1.PTB11, J9.Line_1
  N23: A1.PTE2, J9.Line_2
  N24: A1.PTE3, J9.Line_3
  N25: A1.PTE4, J10.Line_1
  N26: A1.PTE5, J10.Line_2
  N27: A1.VIN, J13.Line_2
  N28: A1.PTB0, J12.Line_1
  N29: A1.PTB1, J12.Line_2
  N30: A1.PTC2, J11.Line_2
  N31: A1.PTC1, J11.Line_3

custom parts:
  FRDM-KL25Z: Freedom Board, based on basic pinout of Arduino Rev.3. Attention: the board is NOT 5V compatible.
  Terminal Block - 3 pins: Generic Screw Terminal 9.5mm
  Terminal Block - 2 pins: Generic Screw Terminal 9.5mm
